// Logisim project minikit_logisim.circ as structural Verilog: 3 circuits, main circuit main
module main (
  input  x,
  input  A,
  input  F,
  input  y,
  input  z,
  input  B,
  input  in_7,
  input  in_8,
  input  in_9,
  input  x_2,
  input  y_2,
  input  in_12,
  input  z_2,
  input  in_14,
  input  in_15,
  input  in_16,
  input  in_17,
  input  in_18,
  input  in_19,
  input  in_20,
  input  in_21,
  input  in_22,
  input  in_23,
  input  in_24,
  input  in_25,
  input  in_26,
  input  in_27,
  input  in_28,
  input  in_29,
  input  in_30,
  input  in_31,
  input  in_32,
  input  in_33,
  input  in_34,
  input  in_35,
  input  in_36,
  input  in_37,
  input  in_38,
  input  in_39,
  input  in_40,
  input  in_41,
  input  in_42,
  input  a_2,
  input  Carry_in,
  input  b_2,
  input  c,
  input  d,
  input  a_3,
  input  b_3,
  input  Carry_in_2,
  input  D0,
  input  A0,
  input  A1,
  input  D1,
  input  D2,
  input  D3,
  input  [1:0] A_4,
  input  s1,
  input  s0,
  input  A0_2,
  input  A0_3,
  input  A1_2,
  input  A1_3,
  input  en1___1,
  input  Enable,
  input  en2a____0,
  input  en2b___0,
  input  [1:0] A_5,
  input  [1:0] A_6,
  input  en1___1_2,
  input  Enable_2,
  input  en2a____0_2,
  input  en2b___0_2,
  input  EN1,
  input  in_75,
  input  in_76,
  input  in_77,
  input  in_78,
  input  in_79,
  input  in_80,
  input  in_81,
  input  in_82,
  input  in_83,
  input  in_84,
  input  EN2A,
  input  EN2B,
  output cout,
  output s,
  output Q0,
  output Q0_2,
  output Q2,
  output Q1,
  output Q1_2,
  output Q3,
  output Q2_2,
  output Q3_2,
  output Q0_3,
  output Q0_4,
  output Q0_5,
  output Q0_6,
  output Q2_3,
  output Q2_4,
  output Q1_3,
  output Q1_4,
  output Q1_5,
  output Q1_6,
  output Q3_3,
  output Q2_5,
  output Q3_4,
  output Q2_6,
  output Q3_5,
  output Q3_6
);

  wire AND_2_out, AND_3_out, AND_4_out, AND_5_out, AND_6_out, AND_7_out, AND_8_out, AND_9_out, AND_10_out,
       AND_11_out, AND_12_out, AND_13_out, AND_14_out, AND_15_out, AND_16_out, AND_17_out, AND_22_out,
       AND_23_out, AND_24_out, AND_25_out, AND_26_out, AND_27_out, AND_28_out, AND_29_out, AND_30_out,
       AND_31_out, AND_32_out, AND_33_out, AND_34_out, AND_35_out, and_36_out, and_37_out, and_38_out,
       and_39_out, and_40_out, and_41_out, and_50_out, and_51_out, and_52_out, and_53_out, and_54_out,
       AND_55_out, and_56_out, and_57_out, AND_58_out, AND_59_out, AND_60_out, AND_61_out, AND_62_out,
       AND_63_out, AND_64_out, AND_65_out, AND_66_out, AND_out, NAND_2_out, NAND_3_out, NAND_4_out,
       NAND_5_out, NAND_6_out, NAND_7_out, NAND_8_out, NAND_9_out, NAND_10_out, NAND_11_out, NAND_12_out,
       NAND_13_out, NAND_14_out, NAND_15_out, nand_16_out, NAND_out, nor_2_out, NOR_out, not_1_out,
       not_2_out, not_3_out, not_4_out, not_5_out, not_6_out, not_7_out, not_8_out, not_9_out, not_10_out,
       not_11_out, not_12_out, not_13_out, not_14_out, not_15_out, not_16_out, not_17_out, not_18_out,
       not_19_out, not_20_out, not_21_out, not_22_out, not_23_out, not_24_out, not_25_out, not_26_out,
       not_27_out, not_28_out, not_29_out, not_30_out, not_31_out, not_32_out, not_33_out, not_34_out,
       not_35_out, not_36_out, not_37_out, not_38_out, not_39_out, not_40_out, not_41_out, not_42_out,
       not_43_out, not_44_out, not_45_out, not_46_out, not_47_out, not_48_out, not_49_out, not_50_out,
       not_51_out, not_52_out, not_53_out, not_54_out, not_55_out, not_56_out, OR_2_out, OR_3_out, or_4_out,
       OR_5_out, OR_6_out, OR_7_out, or_8_out, or_10_out, or_11_out, OR_out, xnor_1_out, xnor_2_out,
       XOR_2_out, XOR_3_out, XOR_4_out, XOR_5_out, xor_6_out, xor_7_out, XOR_out;

  LED led_1 (.in(1'b0));
  LED led_2 (.in(1'b1));
  not not_1 (not_1_out, in_8);
  not not_2 (not_2_out, in_9);
  not not_3 (not_3_out, in_15);
  not not_4 (not_4_out, in_16);
  not not_5 (not_5_out, in_25);
  not not_6 (not_6_out, in_26);
  not not_7 (not_7_out, in_31);
  not not_8 (not_8_out, in_32);
  not not_9 (not_9_out, in_38);
  not not_10 (not_10_out, in_37);
  not not_11 (not_11_out, s1);
  not not_12 (not_12_out, in_75);
  not not_13 (not_13_out, in_76);
  and AND (AND_out, A, B);
  or OR (OR_out, not_1_out, not_2_out);
  nand NAND (NAND_out, in_12, in_14);
  or OR_2 (OR_2_out, not_3_out, not_4_out);
  or OR_3 (OR_3_out, in_21, in_23);
  and AND_2 (AND_2_out, not_5_out, not_6_out);
  nor NOR (NOR_out, in_27, in_29);
  and AND_3 (AND_3_out, not_7_out, not_8_out);
  xor XOR (XOR_out, in_33, in_35);
  and AND_4 (AND_4_out, in_37, not_9_out);
  or or_4 (or_4_out, AND_4_out, AND_5_out);
  and AND_5 (AND_5_out, not_10_out, in_38);
  not not_14 (not_14_out, in_39);
  nand NAND_2 (NAND_2_out, in_40, in_40);
  not not_15 (not_15_out, A0_3);
  not not_16 (not_16_out, A1_3);
  not not_17 (not_17_out, in_77);
  LED led_3 (.in(AND_out));
  not not_18 (not_18_out, OR_out);
  LED led_4 (.in(not_18_out));
  LED led_5 (.in(NAND_out));
  LED led_6 (.in(OR_2_out));
  LED led_7 (.in(OR_3_out));
  not not_19 (not_19_out, AND_2_out);
  LED led_8 (.in(not_19_out));
  LED led_9 (.in(NOR_out));
  LED led_10 (.in(AND_3_out));
  LED led_11 (.in(XOR_out));
  LED led_12 (.in(or_4_out));
  LED led_13 (.in(not_14_out));
  LED led_14 (.in(NAND_2_out));
  xor XOR_2 (XOR_2_out, in_41, in_42);
  xor XOR_3 (XOR_3_out, a_3, b_3);
  and AND_6 (AND_6_out, D0, not_11_out, not_20_out);
  not not_20 (not_20_out, s0);
  and AND_7 (AND_7_out, D1, not_11_out, s0);
  and AND_8 (AND_8_out, D2, s1, not_21_out);
  not not_21 (not_21_out, s0);
  and AND_9 (AND_9_out, D3, s1, s0);
  and AND_10 (AND_10_out, not_12_out, not_13_out, not_17_out);
  and AND_11 (AND_11_out, not_12_out, not_13_out, in_77);
  and AND_12 (AND_12_out, not_12_out, in_76, not_17_out);
  and AND_13 (AND_13_out, not_12_out, in_76, in_77);
  and AND_14 (AND_14_out, in_75, not_13_out, not_17_out);
  and AND_15 (AND_15_out, in_75, not_13_out, in_77);
  and AND_16 (AND_16_out, in_75, in_76, not_17_out);
  and AND_17 (AND_17_out, in_75, in_76, in_77);
  nand NAND_3 (NAND_3_out, F, in_7);
  nand NAND_4 (NAND_4_out, in_28, in_28);
  nand NAND_5 (NAND_5_out, in_30, in_30);
  nand NAND_6 (NAND_6_out, in_34, in_36);
  and AND_18 (Q0_6, not_15_out, Enable_2, not_16_out);
  and AND_19 (Q1_4, A0_3, Enable_2, not_16_out);
  and AND_20 (Q2_6, A1_3, Enable_2, not_15_out);
  and AND_21 (Q3_6, A1_3, Enable_2, A0_3);
  LED F0 (.in(AND_10_out));
  LED F1 (.in(AND_11_out));
  LED F2 (.in(AND_12_out));
  LED F3 (.in(AND_13_out));
  LED F4 (.in(AND_14_out));
  LED F5 (.in(AND_15_out));
  LED F6 (.in(AND_16_out));
  LED F7 (.in(AND_17_out));
  LED led_15 (.in(NAND_7_out));
  nand NAND_7 (NAND_7_out, NAND_3_out, NAND_3_out);
  nand NAND_8 (NAND_8_out, in_22, in_22);
  nand NAND_9 (NAND_9_out, NAND_8_out, NAND_10_out);
  nand NAND_10 (NAND_10_out, in_24, in_24);
  nand NAND_11 (NAND_11_out, NAND_4_out, NAND_5_out);
  nand NAND_12 (NAND_12_out, in_34, NAND_6_out);
  nand NAND_13 (NAND_13_out, NAND_6_out, in_36);
  xor XOR_4 (XOR_4_out, XOR_2_out, Carry_in);
  and AND_22 (AND_22_out, XOR_2_out, Carry_in);
  and AND_23 (AND_23_out, in_41, in_42);
  xor XOR_5 (XOR_5_out, XOR_3_out, Carry_in_2);
  and AND_24 (AND_24_out, b_3, a_3);
  and AND_25 (AND_25_out, b_3, Carry_in_2);
  and AND_26 (AND_26_out, a_3, Carry_in_2);
  or OR_5 (OR_5_out, AND_6_out, AND_7_out, AND_8_out, AND_9_out);
  LED led_16 (.in(OR_5_out));
  Decoder #(.select(2)) decoder_1 (.out0(Q0_3), .out1(Q2_3), .out2(Q1_5), .out3(Q3_3), .sel(A_5), .en(Enable));
  not not_22 (not_22_out, in_78);
  LED led_17 (.in(NAND_9_out));
  LED led_18 (.in(NAND_14_out));
  nand NAND_14 (NAND_14_out, NAND_11_out, NAND_11_out);
  LED led_19 (.in(NAND_15_out));
  nand NAND_15 (NAND_15_out, NAND_12_out, NAND_13_out);
  LED led_20 (.in(XOR_4_out));
  LED led_21 (.in(OR_6_out));
  or OR_6 (OR_6_out, AND_22_out, AND_23_out);
  LED led_22 (.in(XOR_5_out));
  LED led_23 (.in(OR_7_out));
  or OR_7 (OR_7_out, AND_24_out, AND_25_out, AND_26_out);
  not not_23 (not_23_out, in_80);
  not not_24 (not_24_out, in_79);
  not not_25 (not_25_out, A0);
  not not_26 (not_26_out, A1);
  not not_27 (not_27_out, en2a____0_2);
  not not_28 (not_28_out, en2b___0_2);
  and AND_27 (AND_27_out, not_22_out, not_24_out, in_81, not_23_out);
  and AND_28 (AND_28_out, not_22_out, not_24_out, in_81, in_80);
  and AND_29 (AND_29_out, not_22_out, in_79, in_81, not_23_out);
  and AND_30 (AND_30_out, not_22_out, in_79, in_81, in_80);
  and AND_31 (AND_31_out, in_78, not_24_out, in_81, not_23_out);
  and AND_32 (AND_32_out, in_78, not_24_out, in_81, in_80);
  and AND_33 (AND_33_out, in_78, in_79, in_81, not_23_out);
  and AND_34 (AND_34_out, in_78, in_79, in_81, in_80);
  not not_29 (not_29_out, A0_2);
  not not_30 (not_30_out, A1_2);
  and AND_35 (AND_35_out, en1___1_2, not_27_out, not_28_out);
  LED F0_2 (.in(AND_27_out));
  LED F1_2 (.in(AND_28_out));
  LED F2_2 (.in(AND_29_out));
  LED F3_2 (.in(AND_30_out));
  LED F4_2 (.in(AND_31_out));
  LED F5_2 (.in(AND_32_out));
  LED F6_2 (.in(AND_33_out));
  LED F7_2 (.in(AND_34_out));
  and and_36 (and_36_out, a_2, b_2);
  and and_37 (and_37_out, a_2, c);
  and and_38 (and_38_out, b_2, c);
  and and_39 (and_39_out, a_2, d);
  and and_40 (and_40_out, b_2, d);
  and and_41 (and_41_out, c, d);
  xor odd_parity_1 (s, a_2, b_2, c, d);
  and AND_42 (Q0_2, not_25_out, not_26_out);
  and AND_43 (Q1, A0, not_26_out);
  and AND_44 (Q2_2, A1, not_25_out);
  and AND_45 (Q3_2, A1, A0);
  not not_31 (not_31_out, x);
  not not_32 (not_32_out, y);
  not not_33 (not_33_out, z);
  not not_34 (not_34_out, x_2);
  not not_35 (not_35_out, y_2);
  and AND_46 (Q0_4, not_29_out, AND_35_out, not_30_out);
  and AND_47 (Q1_3, A0_2, AND_35_out, not_30_out);
  and AND_48 (Q2_5, A1_2, AND_35_out, not_29_out);
  and AND_49 (Q3_5, A1_2, AND_35_out, A0_2);
  not not_36 (not_36_out, in_83);
  not not_37 (not_37_out, in_82);
  and and_50 (and_50_out, not_31_out, not_32_out, not_33_out);
  not not_38 (not_38_out, x);
  and and_51 (and_51_out, not_38_out, z, not_39_out);
  not not_39 (not_39_out, y);
  and and_52 (and_52_out, not_34_out, y_2);
  or or_8 (or_8_out, x_2, not_35_out, z_2);
  and and_53 (and_53_out, in_17, in_18);
  not not_40 (not_40_out, in_19);
  and and_54 (and_54_out, in_19, not_41_out);
  not not_41 (not_41_out, in_20);
  or or_9 (cout, and_36_out, and_37_out, and_38_out, and_39_out, and_40_out, and_41_out);
  Decoder #(.select(2), .enable("false")) decoder_2 (.out0(Q0), .out1(Q2), .out2(Q1_2), .out3(Q3), .sel(A_4));
  not not_42 (not_42_out, in_84);
  or or_10 (or_10_out, and_50_out, and_51_out);
  not not_43 (not_43_out, and_52_out);
  not not_44 (not_44_out, or_8_out);
  nor nor_2 (nor_2_out, in_17, in_19, in_20);
  xor xor_6 (xor_6_out, in_19, in_20);
  xnor xnor_1 (xnor_1_out, in_17, in_18);
  not not_45 (not_45_out, en2a____0);
  not not_46 (not_46_out, en2b___0);
  and AND_55 (AND_55_out, EN1, not_55_out, not_56_out);
  LED led_24 (.in(or_10_out));
  xnor xnor_2 (xnor_2_out, not_43_out, not_44_out);
  and and_56 (and_56_out, and_53_out, or_11_out);
  or or_11 (or_11_out, not_40_out, xor_6_out);
  and and_57 (and_57_out, xnor_1_out, and_54_out);
  and AND_58 (AND_58_out, en1___1, not_45_out, not_46_out);
  and AND_59 (AND_59_out, not_37_out, not_36_out, AND_55_out, not_42_out);
  not not_47 (not_47_out, AND_59_out);
  and AND_60 (AND_60_out, not_37_out, not_36_out, AND_55_out, in_84);
  not not_48 (not_48_out, AND_60_out);
  not not_49 (not_49_out, AND_61_out);
  and AND_61 (AND_61_out, not_37_out, in_83, AND_55_out, not_42_out);
  not not_50 (not_50_out, AND_62_out);
  and AND_62 (AND_62_out, not_37_out, in_83, AND_55_out, in_84);
  not not_51 (not_51_out, AND_63_out);
  and AND_63 (AND_63_out, in_82, not_36_out, AND_55_out, not_42_out);
  and AND_64 (AND_64_out, in_82, not_36_out, AND_55_out, in_84);
  not not_52 (not_52_out, AND_64_out);
  and AND_65 (AND_65_out, in_82, in_83, AND_55_out, not_42_out);
  not not_53 (not_53_out, AND_65_out);
  not not_54 (not_54_out, AND_66_out);
  and AND_66 (AND_66_out, in_82, in_83, AND_55_out, in_84);
  not not_55 (not_55_out, EN2A);
  not not_56 (not_56_out, EN2B);
  LED led_25 (.in(nand_16_out));
  nand nand_16 (nand_16_out, xnor_2_out, z_2);
  Decoder #(.select(2)) decoder_3 (.out0(Q0_5), .out1(Q2_4), .out2(Q1_6), .out3(Q3_4), .sel(A_6), .en(AND_58_out));
  LED F0_3 (.in(not_47_out));
  LED F1_3 (.in(not_48_out));
  LED F2_3 (.in(not_49_out));
  LED F3_3 (.in(not_50_out));
  LED F4_3 (.in(not_51_out));
  LED F5_3 (.in(not_52_out));
  LED F6_3 (.in(not_53_out));
  LED F7_3 (.in(not_54_out));
  ExactlyOne xor_7 (.out(xor_7_out), .in0(nor_2_out), .in1(and_56_out), .in2(and_57_out));
  LED led_26 (.in(xor_7_out));

  // Notes on the sheet:
  //   Porta Conectivo de Sheffer (NAND)
  //   Não (NOT)
  //   Y
  //   X
  //   Porta E (AND)
  //   Porta OU (OR)
  //   Porta  (NOR)
  //   Porta XOU (XOR)
  //   NOT
  //   Somador Completo de 3 bits
  //   Multiplexador de 4 entradas
  //   Decodificador de 3 entradas e 8 saidas
  //   Z
  //   A.B=F
  //   A+B=F
  //   A=F
  //   Decodificador de 2 entradas e 4 saídas com enable
  //   A+B=F
  //   A⊕B=F
  //   X
  //   input
  //   A
  //   0
  //   0
  //   1
  //   1
  //   A
  //   0
  //   0
  //   1
  //   1
  //   input
  //   A
  //   0
  //   0
  //   1
  //   1
  //   Y
  //   Y
  //   Z
  //   B
  //   0
  //   1
  //   0
  //   1
  //   A.B=F
  //   input
  //   B
  //   0
  //   1
  //   0
  //   1
  //   B
  //   0
  //   1
  //   0
  //   1
  //   input
  //   A
  //   B
  //   0
  //   0
  //   1
  //   0
  //   0
  //   1
  //   1
  //   1
  //   input
  //   A
  //   B
  //   0
  //   0
  //   1
  //   0
  //   0
  //   1
  //   1
  //   1
  //   s
  //   carry out
  //   Decodificador de 3 entradas e 8 saidas com enable
  //   output
  //   F
  //   0
  //   0
  //   0
  //   1
  //   output
  //   F
  //   1
  //   1
  //   1
  //   0
  //   output
  //   F
  //   0
  //   1
  //   1
  //   1
  //   output
  //   F
  //   1
  //   0
  //   0
  //   0
  //   output
  //   F
  //   0
  //   1
  //   1
  //   0
  //   Enable
  //   Decodificador de 2 entradas e 4 saídas
  //   f3
  //   W
  //   Somador  de 4 bits
  //   Decodificador de 2 entradas e 4 saídas com enable de 3
  //   Y
  //   X
  //   Chip 74x138
  //   Z
  //   Enable
endmodule

module aaa (
  input  a,
  input  b,
  input  c,
  input  d,
  output cout,
  output s
);

  wire and_1_out, and_2_out, and_3_out, and_4_out, and_5_out, and_6_out;

  and and_1 (and_1_out, a, b);
  and and_2 (and_2_out, a, c);
  and and_3 (and_3_out, b, c);
  and and_4 (and_4_out, a, d);
  and and_5 (and_5_out, b, d);
  and and_6 (and_6_out, c, d);
  xor odd_parity_1 (s, a, b, c, d);
  or or_1 (cout, and_1_out, and_2_out, and_3_out, and_4_out, and_5_out, and_6_out);
endmodule

module lista_7 (
  input  A0,
  input  A1,
  input  en1___1,
  input  en2a____0,
  input  en2b___0,
  input  [1:0] A,
  input  en1___1_2,
  input  en2a____0_2,
  input  en2b___0_2,
  input  A0_2,
  input  A1_2,
  input  en1___1_3,
  input  en2a____0_3,
  input  en2b___0_3,
  output Q0,
  output Q0_2,
  output Q2,
  output Q1,
  output Q1_2,
  output Q2_2,
  output Q3,
  output Q3_2,
  output Q0_3,
  output Q1_3,
  output Q2_3,
  output Q3_3
);

  wire AND_2_out, AND_7_out, AND_8_out, AND_9_out, AND_10_out, AND_11_out, AND_out, not_1_out, not_2_out,
       not_3_out, not_4_out, not_5_out, not_6_out, not_7_out, not_8_out, not_13_out, not_14_out;

  not not_1 (not_1_out, en2a____0_2);
  not not_2 (not_2_out, en2b___0_2);
  not not_3 (not_3_out, A0);
  not not_4 (not_4_out, A1);
  and AND (AND_out, en1___1_2, not_1_out, not_2_out);
  not not_5 (not_5_out, A0_2);
  not not_6 (not_6_out, A1_2);
  not not_7 (not_7_out, en2a____0_3);
  and AND_2 (AND_2_out, en1___1_3, not_7_out, not_8_out);
  not not_8 (not_8_out, en2b___0_3);
  and AND_3 (Q0, not_3_out, AND_out, not_4_out);
  and AND_4 (Q1, A0, AND_out, not_4_out);
  and AND_5 (Q2_2, A1, AND_out, not_3_out);
  and AND_6 (Q3_2, A1, AND_out, A0);
  and AND_7 (AND_7_out, not_5_out, AND_2_out, not_6_out);
  and AND_8 (AND_8_out, A0_2, AND_2_out, not_6_out);
  and AND_9 (AND_9_out, A1_2, AND_2_out, not_5_out);
  and AND_10 (AND_10_out, A1_2, AND_2_out, A0_2);
  not not_9 (Q0_3, AND_7_out);
  not not_10 (Q1_3, AND_8_out);
  not not_11 (Q2_3, AND_9_out);
  not not_12 (Q3_3, AND_10_out);
  not not_13 (not_13_out, en2a____0);
  not not_14 (not_14_out, en2b___0);
  Decoder #(.select(2)) decoder_1 (.out0(Q0_2), .out1(Q2), .out2(Q1_2), .out3(Q3), .sel(A), .en(AND_11_out));
  and AND_11 (AND_11_out, en1___1, not_13_out, not_14_out);

  // Notes on the sheet:
  //   1)
  //   C)
  //   Enable
  //   Enable
  //   Decodificador de 2 entradas e 4 saídas com enable de 3
  //   D) Saidas do decodificador ativas em nível baixo
  //   Enable
endmodule
